// Logisim project trafficLightController.circ as structural Verilog: 1 circuit, main circuit main
module main (
  input  in_1
);

  wire and_1_out, and_2_out, and_3_out, and_4_out, and_5_out, and_6_out, and_7_out, and_8_out, and_9_out,
       and_10_out, and_11_out, and_12_out, and_13_out, and_14_out, clock_1_out, d_ff_1_q, d_ff_1_qn,
       d_ff_2_q, d_ff_2_qn, d_ff_3_q, d_ff_3_qn, d_ff_4_q, d_ff_4_qn, d_ff_5_q, d_ff_5_qn, d_ff_6_q,
       d_ff_6_qn, not_1_out, not_2_out, or_1_out, or_2_out, or_3_out, or_4_out, or_5_out, or_6_out;

  Clock clock_1 (.out(clock_1_out));
  not not_1 (not_1_out, in_1);
  not not_2 (not_2_out, in_1);
  and and_1 (and_1_out, d_ff_1_q, d_ff_3_q);
  and and_2 (and_2_out, not_2_out, d_ff_5_qn);
  and and_3 (and_3_out, d_ff_4_qn, not_2_out);
  and and_4 (and_4_out, d_ff_4_q, d_ff_6_q);
  and and_5 (and_5_out, not_1_out, d_ff_2_qn);
  and and_6 (and_6_out, d_ff_1_qn, not_1_out);
  or or_1 (or_1_out, and_6_out, d_ff_3_q);
  or or_2 (or_2_out, and_1_out, d_ff_2_qn);
  or or_3 (or_3_out, and_2_out, d_ff_6_qn);
  or or_4 (or_4_out, and_3_out, d_ff_6_q);
  or or_5 (or_5_out, and_4_out, d_ff_5_qn);
  or or_6 (or_6_out, and_5_out, d_ff_3_qn);
  D_Flip_Flop d_ff_1 (.clk(clock_1_out), .D(or_6_out), .Q(d_ff_1_q), .Qn(d_ff_1_qn), .en(1'b1));  // open: preset, reset
  D_Flip_Flop d_ff_2 (.clk(clock_1_out), .D(or_1_out), .Q(d_ff_2_q), .Qn(d_ff_2_qn), .en(1'b1));  // open: preset, reset
  D_Flip_Flop d_ff_3 (.clk(clock_1_out), .D(or_2_out), .Q(d_ff_3_q), .Qn(d_ff_3_qn), .en(1'b1));  // open: preset, reset
  D_Flip_Flop d_ff_4 (.clk(clock_1_out), .D(or_3_out), .Q(d_ff_4_q), .Qn(d_ff_4_qn), .en(1'b1));  // open: preset, reset
  D_Flip_Flop d_ff_5 (.clk(clock_1_out), .D(or_4_out), .Q(d_ff_5_q), .Qn(d_ff_5_qn), .en(1'b1));  // open: preset, reset
  D_Flip_Flop d_ff_6 (.clk(clock_1_out), .D(or_5_out), .Q(d_ff_6_q), .Qn(d_ff_6_qn), .en(1'b1));  // open: preset, reset
  and and_7 (and_7_out, d_ff_1_qn, d_ff_3_qn);
  and and_8 (and_8_out, d_ff_4_qn, d_ff_6_qn);
  and and_9 (and_9_out, d_ff_5_qn, d_ff_6_q);
  and and_10 (and_10_out, d_ff_2_qn, d_ff_3_q);
  and and_11 (and_11_out, d_ff_1_qn, d_ff_3_q);
  and and_12 (and_12_out, d_ff_2_qn, d_ff_3_qn);
  and and_13 (and_13_out, d_ff_4_qn, d_ff_6_q);
  and and_14 (and_14_out, d_ff_5_qn, d_ff_6_qn);
  LED led_1 (.in(d_ff_2_q));
  LED led_2 (.in(and_10_out));
  LED led_3 (.in(and_12_out));
  LED led_4 (.in(d_ff_1_q));
  LED led_5 (.in(and_7_out));
  LED led_6 (.in(and_11_out));
  LED led_7 (.in(d_ff_4_q));
  LED led_8 (.in(and_8_out));
  LED led_9 (.in(and_13_out));
  LED led_10 (.in(d_ff_5_q));
  LED led_11 (.in(and_9_out));
  LED led_12 (.in(and_14_out));

  // Notes on the sheet:
  //   :
  //   :
  //   -
  //   -
  //   R2
  //   Y2
  //   G2
  //   R1
  //   Y1
  //   G1
  //   R3
  //   Y3
  //   G3
  //   R4
  //   Y4
  //   G4
endmodule
